// Logisim project CPU.circ as structural Verilog: 21 circuits, main circuit main
module main (
  input  Reset_counter,
  input  Clear_memory,
  input  clear,
  input  Clear_2,
  output [3:0] Opcode,
  output [2:0] rs,
  output [2:0] rt,
  output [2:0] rd,
  output [2:0] out_9,
  output [2:0] out_10,
  output [15:0] out_11,
  output [2:0] out_12,
  output [15:0] out_13,
  output [2:0] out_14,
  output [15:0] out_15
);

  wire and_2_out, clock, clock_1_out, control_unit_1_alusrc, control_unit_1_branch, control_unit_1_jump,
       control_unit_1_memread, control_unit_1_memtoreg, control_unit_1_memwrite, control_unit_1_regdst,
       control_unit_1_regwrite, halt, ra, rtn, zero;
  wire [2:0] alu_control_1_opout, multiplexer_3_out;
  wire [15:0] adder_2_out, adress, alu_1_out_4, Data_2, multiplexer_1_out, multiplexer_2_out,
       multiplexer_4_out, multiplexer_5_out, multiplexer_6_out, PC_q, ram_2_data, read_ra, Shift;

  Clock clock_1 (.out(clock_1_out));
  Register #(.width(16), .trigger("falling")) PC (
    .D(multiplexer_6_out), .en(1'b1), .Q(PC_q), .clk(clock), .clr(Reset_counter));
  Adder #(.width(16)) adder_1 (.a(PC_q), .b(16'h1), .out(adress));  // open: cin, cout
  and and_1 (clock, clock_1_out, ~halt);  // AND_Gate
  RAM #(.addrWidth(16), .dataWidth(16)) ram_1 (
    .addr(PC_q), .data({Opcode, rs, rt, rd, out_10}), .sel(1'b1), .clr(Clear_memory));  // open: clk, ld
  Adder #(.width(16)) adder_2 (.a(PC_q), .b(Shift), .out(adder_2_out));  // open: cin, cout
  Multiplexer #(.width(16), .enable("false")) multiplexer_1 (
    .in0(adress), .in1(adder_2_out), .out(multiplexer_1_out), .sel(and_2_out));
  Multiplexer #(.width(16), .enable("false")) multiplexer_2 (
    .in0(multiplexer_1_out), .in1(adder_2_out), .out(multiplexer_2_out), .sel(control_unit_1_jump));
  Control_unit control_unit_1 (
    .in_1(Opcode), .RegDst(control_unit_1_regdst), .ALUsrc(control_unit_1_alusrc),
    .MemtoReg(control_unit_1_memtoreg), .RegWrite(control_unit_1_regwrite), .MemRead(control_unit_1_memread),
    .MemWrite(control_unit_1_memwrite), .ALUOp(out_9), .halt(halt), .Branch(control_unit_1_branch),
    .Jump(control_unit_1_jump), .call(ra), .\return (rtn));
  Multiplexer #(.width(3), .enable("false")) multiplexer_3 (
    .in0(rt), .in1(rd), .out(multiplexer_3_out), .sel(control_unit_1_regdst));
  Multiplexer #(.width(16), .enable("false")) multiplexer_4 (
    .in0(out_13), .in1(adress), .out(multiplexer_4_out), .sel(ra));
  Multiplexer #(.width(16), .enable("false")) multiplexer_5 (
    .in0(multiplexer_2_out), .in1(adder_2_out), .out(multiplexer_5_out), .sel(ra));
  Multiplexer #(.width(16), .enable("false")) multiplexer_6 (
    .in0(multiplexer_5_out), .in1(read_ra), .out(multiplexer_6_out), .sel(rtn));
  and and_2 (and_2_out, zero, control_unit_1_branch);
  _16_bit_register u_16_bit_register_1 (
    .Write_register(multiplexer_3_out), .Register_data(multiplexer_4_out), .read_data_1(out_11),
    .read_data_2(Data_2), .Clock_input(clock), .clear(Clear_2), .Read_register_2(rt), .Read_register_1(rs),
    .Write_enabled(control_unit_1_regwrite), .in_1(ra), .read_ra_register(read_ra));
  assign Shift = {{10{rd[2]}}, {rd, out_10}};  // Bit_Extender bit_extender_1
  Multiplexer #(.width(16), .enable("false")) multiplexer_7 (
    .in0(Data_2), .in1(Shift), .out(out_15), .sel(control_unit_1_alusrc));
  ALU_control alu_control_1 (.ALUOP(out_9), .Func(out_10), .OPout(alu_control_1_opout));
  RAM #(.addrWidth(16), .dataWidth(16), .bus("separate")) ram_2 (
    .addr(alu_1_out_4), .din(Data_2), .data(ram_2_data), .str(control_unit_1_memwrite), .sel(1'b1),
    .clk(clock), .ld(control_unit_1_memread), .clr(clear));
  ALU alu_1 (.in_1(out_11), .in_2(out_15), .Mux_select(alu_control_1_opout), .out_4(alu_1_out_4), .zero(zero));
  Multiplexer #(.width(16), .enable("false")) multiplexer_8 (
    .in0(alu_1_out_4), .in1(ram_2_data), .out(out_13), .sel(control_unit_1_memtoreg));

  assign out_12 = out_9;
  assign out_14 = out_10;

  // Other names for the same wires on the sheet: Bit_in[5:0] = {rd, out_10}; Write_data[15:0] = out_13

  // Notes on the sheet:
  //   immediate
endmodule

module _16_bit_register (
  input  in_1,
  input  Write_enabled,
  input  [2:0] Write_register,
  input  [15:0] Register_data,
  input  [2:0] Read_register_2,
  input  [2:0] Read_register_1,
  input  Clock_input,
  input  clear,
  output [15:0] read_ra_register,
  output [15:0] read_data_1,
  output [15:0] read_data_2
);

  wire and_1_out, and_2_out, and_3_out, and_4_out, and_5_out, and_6_out, and_7_out, and_8_out,
       decoder_1_out0, decoder_1_out1, decoder_1_out2, decoder_1_out3, decoder_1_out4, decoder_1_out5,
       decoder_1_out6, decoder_1_out7;
  wire [15:0] r7_q, register_2_q, register_3_q, register_4_q, register_5_q, register_6_q, register_7_q,
       register_8_q;

  Decoder #(.select(3), .enable("false")) decoder_1 (
    .out0(decoder_1_out0), .out1(decoder_1_out1), .out2(decoder_1_out2), .out3(decoder_1_out3),
    .out4(decoder_1_out4), .out5(decoder_1_out5), .out6(decoder_1_out6), .out7(decoder_1_out7),
    .sel(Write_register));
  and and_1 (and_1_out, Write_enabled, decoder_1_out0);
  and and_2 (and_2_out, Write_enabled, decoder_1_out1);
  and and_3 (and_3_out, Write_enabled, decoder_1_out2);
  and and_4 (and_4_out, Write_enabled, decoder_1_out3);
  and and_5 (and_5_out, Write_enabled, decoder_1_out4);
  and and_6 (and_6_out, Write_enabled, decoder_1_out5);
  and and_7 (and_7_out, Write_enabled, decoder_1_out6);
  and and_8 (and_8_out, Write_enabled, decoder_1_out7);
  Register #(.width(16)) register_1 (
    .D(Register_data), .en(in_1), .Q(read_ra_register), .clk(Clock_input), .clr(clear));
  Register #(.width(16)) register_2 (
    .D(Register_data), .en(and_1_out), .Q(register_2_q), .clk(Clock_input), .clr(clear));
  Register #(.width(16)) register_3 (
    .D(Register_data), .en(and_2_out), .Q(register_3_q), .clk(Clock_input), .clr(clear));
  Register #(.width(16)) register_4 (
    .D(Register_data), .en(and_3_out), .Q(register_4_q), .clk(Clock_input), .clr(clear));
  Register #(.width(16)) register_5 (
    .D(Register_data), .en(and_4_out), .Q(register_5_q), .clk(Clock_input), .clr(clear));
  Register #(.width(16)) register_6 (
    .D(Register_data), .en(and_5_out), .Q(register_6_q), .clk(Clock_input), .clr(clear));
  Register #(.width(16)) register_7 (
    .D(Register_data), .en(and_6_out), .Q(register_7_q), .clk(Clock_input), .clr(clear));
  Register #(.width(16)) register_8 (
    .D(Register_data), .en(and_7_out), .Q(register_8_q), .clk(Clock_input), .clr(clear));
  Register #(.width(16)) r7 (.D(Register_data), .en(and_8_out), .Q(r7_q), .clk(Clock_input), .clr(clear));
  Multiplexer #(.select(3), .width(16), .enable("false")) multiplexer_1 (
    .in0(register_2_q), .in1(register_3_q), .in2(register_4_q), .in3(register_5_q), .in4(register_6_q),
    .in5(register_7_q), .in6(register_8_q), .in7(r7_q), .out(read_data_1), .sel(Read_register_1));
  Multiplexer #(.select(3), .width(16), .enable("false")) multiplexer_2 (
    .in0(register_2_q), .in1(register_3_q), .in2(register_4_q), .in3(register_5_q), .in4(register_6_q),
    .in5(register_7_q), .in6(register_8_q), .in7(r7_q), .out(read_data_2), .sel(Read_register_2));

  // Notes on the sheet:
  //   write enabled for ra
  //   ra
  //   r8
  //   r1
  //   r2
  //   r3
  //   r4
  //   r5
  //   r6
endmodule

module ALU (
  input  [15:0] in_1,
  input  [15:0] in_2,
  input  [2:0] Mux_select,
  output [15:0] out_4,
  output zero
);

  wire comparator_1_eq, comparator_1_lt, comparator_2_eq, not_1_out, or_2_out;
  wire [15:0] adder_1_out, and_1_out, or_1_out;

  Comparator #(.width(16)) comparator_1 (.a(in_1), .b(in_2), .eq(comparator_1_eq), .lt(comparator_1_lt));  // open: gt
  Comparator #(.width(16)) comparator_2 (.a(in_1), .b(in_2), .eq(comparator_2_eq));  // open: gt, lt
  Adder #(.width(16)) adder_1 (.a(in_1), .b(in_2), .out(adder_1_out));  // open: cin, cout
  assign and_1_out = in_1 & in_2;  // AND_Gate and_1, 16 bits wide
  assign or_1_out = in_1 | in_2;  // OR_Gate or_1, 16 bits wide
  not not_1 (not_1_out, comparator_2_eq);
  or or_2 (or_2_out, comparator_1_eq, comparator_1_lt);
  Multiplexer #(.select(3), .width(16), .enable("false")) multiplexer_1 (
    .in1(adder_1_out), .in2(and_1_out), .in3(or_1_out), .in4(in_2), .in5(in_1), .out(out_4), .sel(Mux_select));  // open: in0, in6, in7
  Multiplexer #(.select(3), .enable("false")) multiplexer_2 (
    .in6(or_2_out), .in7(not_1_out), .out(zero), .sel(Mux_select));  // open: in0, in1, in2, in3, in4, in5

  // Other names for the same wires on the sheet: I1[15:0] = in_1; I2[15:0] = in_2

  // Notes on the sheet:
  //   input 1
  //   input 2
  //   if(  r1 <= r2 ) ->1 
  //   if( r1 != r2 ) -> 1
  //   else () ->0
  //   output
endmodule

module Control_unit (
  input  [3:0] in_1,
  output Jump,
  output RegDst,
  output Branch,
  output MemRead,
  output MemtoReg,
  output [2:0] ALUOp,
  output MemWrite,
  output ALUsrc,
  output RegWrite,
  output halt,
  output call,
  output \return 
);

  Jump jump_1 (.in_1(in_1), .out_2(Jump));
  Regdest regdest_1 (.in_1(in_1), .out_2(RegDst));
  Branch branch_1 (.in_1(in_1), .out_2(Branch));
  MemRead memread_1 (.in_1(in_1), .out_2(MemRead));
  MemtoReg memtoreg_1 (.in_1(in_1), .out_2(MemtoReg));
  ALUop aluop_1 (.in_1(in_1), .out_2(ALUOp));
  MemWrite memwrite_1 (.in_1(in_1), .out_2(MemWrite));
  ALUsrc alusrc_1 (.in_1(in_1), .out_2(ALUsrc));
  Regwrite regwrite_1 (.in_1(in_1), .out_2(RegWrite));
  Halt halt_1 (.in_1(in_1), .out_2(halt));
  call call_1 (.in_1(in_1), .out_2(call));
  \return  return_1 (.in_1(in_1), .out_2(\return ));
endmodule

module ALU_control (
  input  [2:0] ALUOP,
  input  [2:0] Func,
  output [2:0] OPout
);

  wire and_1_out, and_2_out, and_3_out, and_4_out, and_5_out, and_6_out, and_7_out, and_8_out, and_9_out,
       and_10_out, and_11_out, and_12_out, and_13_out, and_14_out, and_15_out, and_16_out;
  wire [2:0] multiplexer_1_out;

  Multiplexer #(.select(3), .width(3), .enable("false")) multiplexer_1 (
    .in0(Func), .in1(3'b000), .in2(3'b000), .in3(3'b000), .in4(3'b000), .in5(3'b000), .in6(3'b000),
    .in7(3'b000), .out(multiplexer_1_out), .sel(ALUOP));
  and and_1 (and_1_out, ALUOP[2], ~ALUOP[1], ~ALUOP[0]);  // AND_Gate
  and and_2 (and_2_out, ALUOP[2], ~ALUOP[1], ALUOP[0]);  // AND_Gate
  and and_3 (and_3_out, ALUOP[2], ALUOP[1], ~ALUOP[0]);  // AND_Gate
  and and_4 (and_4_out, ALUOP[2], ALUOP[1], ALUOP[0]);
  and and_5 (and_5_out, ~ALUOP[2], ~ALUOP[1], ~ALUOP[0], ~multiplexer_1_out[2], multiplexer_1_out[1], ~multiplexer_1_out[0]);  // AND_Gate
  and and_6 (and_6_out, ~ALUOP[2], ~ALUOP[1], ~ALUOP[0], ~multiplexer_1_out[2], multiplexer_1_out[1], multiplexer_1_out[0]);  // AND_Gate
  and and_7 (and_7_out, ~ALUOP[2], ALUOP[1], ~ALUOP[0]);  // AND_Gate
  and and_8 (and_8_out, ~ALUOP[2], ALUOP[1], ALUOP[0]);  // AND_Gate
  and and_9 (and_9_out, ALUOP[2], ALUOP[1], ~ALUOP[0]);  // AND_Gate
  and and_10 (and_10_out, ALUOP[2], ALUOP[1], ALUOP[0]);
  and and_11 (and_11_out, ~ALUOP[2], ~ALUOP[1], ~ALUOP[0], ~multiplexer_1_out[2], ~multiplexer_1_out[1], multiplexer_1_out[0]);  // AND_Gate
  and and_12 (and_12_out, ~ALUOP[2], ~ALUOP[1], ~ALUOP[0], ~multiplexer_1_out[2], multiplexer_1_out[1], multiplexer_1_out[0]);  // AND_Gate
  and and_13 (and_13_out, ~ALUOP[2], ~ALUOP[1], ALUOP[0]);  // AND_Gate
  and and_14 (and_14_out, ALUOP[2], ~ALUOP[1], ALUOP[0]);  // AND_Gate
  and and_15 (and_15_out, ~ALUOP[2], ALUOP[1], ALUOP[0]);  // AND_Gate
  and and_16 (and_16_out, ALUOP[2], ALUOP[1], ALUOP[0]);
  or or_1 (OPout[2], and_1_out, and_2_out, and_3_out, and_4_out);
  or or_2 (OPout[1], and_5_out, and_6_out, and_7_out, and_8_out, and_9_out, and_10_out);
  or or_3 (OPout[0], and_11_out, and_12_out, and_13_out, and_14_out, and_15_out, and_16_out);
endmodule

module Regwrite (
  input  [3:0] in_1,
  output out_2
);

  wire and_1_out, and_2_out, and_3_out, and_4_out, and_5_out, and_6_out, and_7_out, and_8_out, and_9_out;

  and and_1 (and_1_out, ~in_1[3], ~in_1[2], ~in_1[1], in_1[0]);  // AND_Gate
  and and_2 (and_2_out, ~in_1[3], in_1[2], in_1[1], ~in_1[0]);  // AND_Gate
  and and_3 (and_3_out, in_1[3], in_1[2], in_1[1], in_1[0]);
  and and_4 (and_4_out, ~in_1[3], ~in_1[2], ~in_1[1], ~in_1[0]);  // AND_Gate
  and and_5 (and_5_out, ~in_1[3], ~in_1[2], in_1[1], ~in_1[0]);  // AND_Gate
  and and_6 (and_6_out, ~in_1[3], in_1[2], ~in_1[1], ~in_1[0]);  // AND_Gate
  and and_7 (and_7_out, ~in_1[3], in_1[2], ~in_1[1], in_1[0]);  // AND_Gate
  and and_8 (and_8_out, ~in_1[3], in_1[2], in_1[1], in_1[0]);  // AND_Gate
  and and_9 (and_9_out, in_1[3], ~in_1[2], ~in_1[1], ~in_1[0]);  // AND_Gate
  or or_1 (out_2, and_1_out, and_2_out, and_3_out, and_4_out, and_5_out, and_6_out, and_7_out, and_8_out, and_9_out);
endmodule

module Regdest (
  input  [3:0] in_1,
  output out_2
);

  wire and_1_out, and_2_out, and_3_out;

  and and_1 (and_1_out, ~in_1[0], in_1[1], in_1[2], ~in_1[3]);  // AND_Gate
  and and_2 (and_2_out, in_1[0], in_1[1], in_1[2], in_1[3]);
  and and_3 (and_3_out, ~in_1[0], ~in_1[1], ~in_1[2], ~in_1[3]);  // AND_Gate
  or or_1 (out_2, and_1_out, and_2_out, and_3_out);
endmodule

module ALUsrc (
  input  [3:0] in_1,
  output out_2
);

  wire and_1_out, and_2_out, and_3_out, and_4_out, and_5_out;

  and and_1 (and_1_out, ~in_1[3], ~in_1[2], in_1[1]);  // AND_Gate
  and and_2 (and_2_out, ~in_1[3], in_1[2], ~in_1[1], in_1[0]);  // AND_Gate
  and and_3 (and_3_out, ~in_1[3], in_1[2], in_1[1], in_1[0]);  // AND_Gate
  and and_4 (and_4_out, in_1[3], ~in_1[2], ~in_1[1], ~in_1[0]);  // AND_Gate
  and and_5 (and_5_out, ~in_1[3], ~in_1[2], ~in_1[1], in_1[0]);  // AND_Gate
  or or_1 (out_2, and_1_out, and_2_out, and_3_out, and_4_out, and_5_out);
endmodule

module Halt (
  input  [3:0] in_1,
  output out_2
);

  and and_1 (out_2, in_1[3], in_1[2], in_1[1], ~in_1[0]);  // AND_Gate
endmodule

module MemtoReg (
  input  [3:0] in_1,
  output out_2
);

  and and_1 (out_2, ~in_1[3], ~in_1[2], in_1[1], ~in_1[0]);  // AND_Gate
endmodule

module MemRead (
  input  [3:0] in_1,
  output out_2
);

  and and_1 (out_2, ~in_1[3], ~in_1[2], in_1[1], ~in_1[0]);  // AND_Gate
endmodule

module MemWrite (
  input  [3:0] in_1,
  output out_2
);

  and and_1 (out_2, ~in_1[3], ~in_1[2], in_1[1], in_1[0]);  // AND_Gate
endmodule

module Branch (
  input  [3:0] in_1,
  output out_2
);

  wire and_1_out, and_2_out;

  and and_1 (and_1_out, in_1[3], ~in_1[2], ~in_1[1], in_1[0]);  // AND_Gate
  and and_2 (and_2_out, in_1[3], ~in_1[2], in_1[1], ~in_1[0]);  // AND_Gate
  or or_1 (out_2, and_1_out, and_2_out);
endmodule

module Jump (
  input  [3:0] in_1,
  output out_2
);

  and and_1 (out_2, in_1[3], ~in_1[2], in_1[1], in_1[0]);  // AND_Gate
endmodule

module ALUop (
  input  [3:0] in_1,
  output [2:0] out_2
);

  ALUop1 aluop1_1 (.in_1(in_1), .out_2(out_2[2]));
  ALUop2 aluop2_1 (.in_1(in_1), .out_2(out_2[1]));
  ALUop3 aluop3_1 (.in_1(in_1), .out_2(out_2[0]));
endmodule

module ALUop1 (
  input  [3:0] in_1,
  output out_2
);

  wire and_1_out, and_2_out, and_3_out, and_4_out;

  and and_1 (and_1_out, ~in_1[3], ~in_1[2], ~in_1[1], in_1[0]);  // AND_Gate
  and and_2 (and_2_out, ~in_1[3], in_1[2], ~in_1[1], ~in_1[0]);  // AND_Gate
  and and_3 (and_3_out, in_1[3], ~in_1[2], ~in_1[1], in_1[0]);  // AND_Gate
  and and_4 (and_4_out, in_1[3], ~in_1[2], in_1[1], ~in_1[0]);  // AND_Gate
  or or_1 (out_2, and_1_out, and_2_out, and_3_out, and_4_out);
endmodule

module ALUop2 (
  input  [3:0] in_1,
  output out_2
);

  wire and_1_out, and_2_out, and_3_out, and_4_out;

  and and_1 (and_1_out, ~in_1[3], in_1[2], in_1[1], in_1[0]);  // AND_Gate
  and and_2 (and_2_out, in_1[3], ~in_1[2], ~in_1[1], ~in_1[0]);  // AND_Gate
  and and_3 (and_3_out, in_1[3], ~in_1[2], ~in_1[1], in_1[0]);  // AND_Gate
  and and_4 (and_4_out, in_1[3], ~in_1[2], in_1[1], ~in_1[0]);  // AND_Gate
  or or_1 (out_2, and_1_out, and_2_out, and_3_out, and_4_out);
endmodule

module ALUop3 (
  input  [3:0] in_1,
  output out_2
);

  wire and_1_out, and_2_out, and_3_out, and_4_out, and_5_out, and_6_out;

  and and_1 (and_1_out, ~in_1[3], ~in_1[2], in_1[1], ~in_1[0]);  // AND_Gate
  and and_2 (and_2_out, ~in_1[3], ~in_1[2], in_1[1], in_1[0]);  // AND_Gate
  and and_3 (and_3_out, ~in_1[3], in_1[2], ~in_1[1], ~in_1[0]);  // AND_Gate
  and and_4 (and_4_out, ~in_1[3], in_1[2], ~in_1[1], in_1[0]);  // AND_Gate
  and and_5 (and_5_out, in_1[3], ~in_1[2], ~in_1[1], ~in_1[0]);  // AND_Gate
  and and_6 (and_6_out, in_1[3], ~in_1[2], in_1[1], ~in_1[0]);  // AND_Gate
  or or_1 (out_2, and_1_out, and_2_out, and_3_out, and_4_out, and_5_out, and_6_out);
endmodule

module cOp1 (
  input  [2:0] ALUOP,
  input  [2:0] in_2
);
endmodule

module call (
  input  [3:0] in_1,
  output out_2
);

  and and_1 (out_2, in_1[3], in_1[2], ~in_1[1], ~in_1[0]);  // AND_Gate
endmodule

module \return  (
  input  [3:0] in_1,
  output out_2
);

  and and_1 (out_2, in_1[3], in_1[2], ~in_1[1], in_1[0]);  // AND_Gate
endmodule
